# Fritzing sketch Untitled modulo01 (saved by Fritzing 0.7.5b)
breadboards: 1

parts:
  Arduino1 = Arduino
  LED1 = LED - 5mm [color="Red (633nm)" package="5 mm [THT]"]
  R1 = Resistor [tolerance=±5% resistance=220 package=THT]
  R2 = Resistor [tolerance=±5% resistance=220 package=THT]
  S1 = Pushbutton [package="[THT]"]

nets:
  N1: Arduino1.aref, R1.Pin_0
  N2: Arduino1.D2, R2.Pin_0, S1.Pin_1, S1.Pin_2
  N3: Arduino1.RST, S1.Pin_3, S1.Pin_4
  N4: Arduino1.3V3, LED1.anode
  N5: Arduino1.+5V, R2.Pin_1
  N6: LED1.cathode, R1.Pin_1

// code stored in the sketch: modulo01.ino
/********************************
  ROBOCORE ARDUINO KIT INICIANTE
  Modulo 1
********************************/
int ledPin = 13;    //led pino 13
int botao = 2;      //botao no pino 2
int estadoBotao = 0;//vairavel para ler o status do push button

void setup(){
  pinMode (ledPin, OUTPUT);  //pino do led sera saida
  pinMode (botao, INPUT);    //pino com botao sera entrada
  
}

void loop(){
  estadoBotao = digitalRead(botao); 
      /* novo estado do botao vai ser igual ao que Arduino ler no pino onde 
      esta o botao. Podera ser ALTO (HIGH) se o botao estiver pressionado
      ou BAIXO (LOW) se o botao estiver solto*/
      
  if (estadoBotao == HIGH){
     digitalWrite(ledPin, HIGH); 
    
  }else{
    digitalWrite(ledPin, LOW);
    
  }
}
